# Fritzing sketch Ultrasonuic (saved by Fritzing 0.9.3b)
breadboards: 1

parts:
  D1 = LTE-302 [package=lte-302]
  R1 = Resistor [tolerance=±5% resistance=220 package="0603 [SMD]"]
  HC-SR04_Sensor_1 = HC-SR04 Ultrasonic Distance Sensor
  Part1 = Arduino Leonardo (Rev3b)

nets:
  GND: D1.A, HC-SR04_Sensor_1.GND, Part1.GND
  N1: D1.C, R1.Pin_1
  N2: R1.Pin_0, Part1.D10_PWM/A10
  VCC: HC-SR04_Sensor_1.VCC, Part1.VIN
  N3: HC-SR04_Sensor_1.TRIG, Part1.D8/A8
  N4: HC-SR04_Sensor_1.ECHO, Part1.D9_PWM/A9
